// Logisim project ex3.circ as structural Verilog: 1 circuit, main circuit AddMachine
module AddMachine (
  input  clk,
  output [7:0] ADD_OUT,
  output [7:0] REG_OUT
);

  wire [7:0] undriven;

  Adder adder_1 (.a(undriven), .b(REG_OUT), .out(ADD_OUT));  // open: cin, cout
  Register register_1 (.clk(clk), .Q(REG_OUT));  // open: D, en, clr
endmodule
